# Fritzing sketch ws-display (saved by Fritzing 0.9.2b)

parts:
  Part1 = Arduino Nano (Rev3.0) (ICSP)
  R1 = Resistor [tolerance=±5% resistance=220 package="1206 [SMD]"]
  R2 = Resistor [tolerance=±5% resistance=220 package="1206 [SMD]"]
  R3 = Resistor [tolerance=±5% resistance=220 package="0402 [SMD]"]
  R4 = Resistor [tolerance=±5% resistance=220 package="1206 [SMD]"]
  7_Segment_4_Digit_Display1 = 7-SEGMENT-4DIGIT common cathode

nets:
  N1: Part1.D2, 7_Segment_4_Digit_Display1.pin_7
  N2: Part1.D3, 7_Segment_4_Digit_Display1.pin_8
  N3: Part1.D4, 7_Segment_4_Digit_Display1.pin_10
  N4: Part1.D5, 7_Segment_4_Digit_Display1.pin_11
  N5: Part1.D6, 7_Segment_4_Digit_Display1.pin_6
  N6: Part1.D7, 7_Segment_4_Digit_Display1.pin_2
  N7: Part1.D8, R4.Pin_0
  N8: Part1.D9, R2.Pin_0
  N9: Part1.D10, R1.Pin_0
  N10: Part1.D11/MOSI, R3.Pin_1
  N11: Part1.A1, 7_Segment_4_Digit_Display1.pin_9
  N12: Part1.A0, 7_Segment_4_Digit_Display1.pin_3
  N13: R1.Pin_1, 7_Segment_4_Digit_Display1.pin_5
  N14: R2.Pin_1, 7_Segment_4_Digit_Display1.pin_4
  N15: R3.Pin_0, 7_Segment_4_Digit_Display1.pin_12
  N16: R4.Pin_1, 7_Segment_4_Digit_Display1.pin_1

custom parts:
  7-SEGMENT-4DIGIT common cathode: A 7 Segment 4 Digit common anode display, with decimal points
